# Fritzing sketch LimboRadio (saved by Fritzing 0.9.3b)
circuit board: 7.5cm x 7.5cm
breadboards: 1

parts:
  Bauteil1 = Adafruit MAX98357A I2S 3W Class D Amplifier [part_number="Adafruit #3006"]
  RotEnc = Rotary Encoder with Knob
  OLED = OLED 0.96" 128x64 I2C SSD1306
  PIR1 = PIR sensor
  Bauteil2 = Barometric Pressure Sensor - BMP180 Breakout (GY-68)
  J1 = shrouded pin header, 40 pins [form="♂ (shrouded male)"]
  R1 = Resistor [tolerance=±5% resistance=220 package=THT]
  R2 = Resistor [tolerance=±5% resistance=220 package=THT]
  J3 = female pin header, 4 pins [form="♀ (female)"]
  R4 = Resistor [tolerance=±5% resistance=220 package=THT]
  J4 = Screw terminal - 2 pins [package=THT]
  R5 = Resistor [tolerance=±5% resistance=220 package=THT]
  J5 = female pin header, 4 pins [form="♀ (female)"]

nets:
  N1: Bauteil1.VIN, J1.pin3
  N2: Bauteil1.GND, J1.pin26
  N3: Bauteil1.SD_MODE, J1.pin40
  N4: Bauteil1.GAIN, R5.Pin_0
  N5: Bauteil1.BCLK, J1.pin23, J4.pin2, R5.Pin_1
  N6: Bauteil1.LRCLK, PIR1.SIG, J1.pin21, J4.pin1
  N7: RotEnc.no_name_yet#1, J1.pin14, R2.Pin_1
  N8: RotEnc.no_name_yet#2, RotEnc.no_name_yet#4, PIR1.VDD, J1.pin8
  N9: RotEnc.no_name_yet#3, J1.pin13, R1.Pin_1
  N10: RotEnc.no_name_yet#5, J1.pin2, R4.Pin_0
  N11: OLED.VCC, J1.pin27, J3.pin3
  N12: OLED.GND, J1.pin12, J3.pin4
  N13: OLED.SCL, J1.pin34, J3.pin2
  N14: OLED.SCA, J1.pin7, J3.pin1
  N15: PIR1.GND, J1.pin15
  N16: Bauteil2.VCC, J5.pin1
  N17: Bauteil2.GND, J1.pin16, J5.pin2
  N18: Bauteil2.SCL, J1.pin18, J5.pin3
  N19: Bauteil2.SDA, J1.pin19, J5.pin4
  N20: J1.pin20, R1.Pin_0, R2.Pin_0, R4.Pin_1

notes:
  5V
  GND
  GND 3V  SCK SDA
  SDA SCK GND 3V
  SIG 5V GND
  LRC CLK DIN GAIN SD GND 5V

custom parts:
  Adafruit MAX98357A I2S 3W Class D Amplifier: Listen to this good news - we now have an all in one digital audio amp breakout board that works incredibly well with the Raspberry Pi! If you're looking for an easy and low cost way to get you digital sound files bumpin' then the MAX08357 I2S Amp Breakout is for you. It takes standard I2S digital audio input and, not only decodes it into analog, but also amplifies it directly into a speaker.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
  Rotary Encoder with Knob: Rotary Encoder with 1/4" Shaft and Knob
